# Fritzing sketch sketch (saved by Fritzing 0.9.1b)
stripboards: 1

parts:
  Arduino_Nano_V3 = Arduino Nano (Rev3.0)
  Easy_Driver_(Sparkfun) = EasyDriver_v44
  Lipo_2cells_(7_4V) = Power plug
  Stepper_1_8° = Stepper Motor - Bipolar
  LED_témoin = LED - 5mm [color="Red (633nm)" package="5 mm [THT]"]
  Joystick_+_Push_bt = Thumb Joystick
  S1 = Pushbutton [package=THT]
  Switch_CW_or_CCW = Pushbutton [package=THT]
  Pot_max_speed = Rotary Potentiometer (Small) [maximum_resistance=10kΩ package=THT]
  R1 = Resistor [tolerance=±5% resistance=220 package=THT]
  U1 = MIDI_CONN_FEMALE [package=din_5_female]
  U2 = MIDI_CONN_FEMALE [package=din_5_female]
  U3 = MIDI_CONN_FEMALE [package=din_5_female]
  U4 = MIDI_CONN_FEMALE [package=din_5_female]

nets:
  N1: Arduino_Nano_V3.D4, Easy_Driver_(Sparkfun).DIR
  N2: Arduino_Nano_V3.D5, Easy_Driver_(Sparkfun).STEP
  N3: Arduino_Nano_V3.D6, Switch_CW_or_CCW.leg1
  N4: Arduino_Nano_V3.D7, R1.Pin_0
  N5: Arduino_Nano_V3.D8, U1.MIDI_IN
  GND: Arduino_Nano_V3.GND, Easy_Driver_(Sparkfun).GND, LED_témoin.cathode, S1.leg0, Switch_CW_or_CCW.leg0, Pot_max_speed.leg2, U1.NC2
  5V: Arduino_Nano_V3.5V, Easy_Driver_(Sparkfun).VCC, Pot_max_speed.leg1, U1.NC3
  N6: Arduino_Nano_V3.A7, Pot_max_speed.wiper
  N7: Arduino_Nano_V3.A6, U1.MIDI_OUT
  N8: Easy_Driver_(Sparkfun).V+, Lipo_2cells_(7_4V).VCC
  N9: Easy_Driver_(Sparkfun).OUT2A, U4.NC3
  N10: Easy_Driver_(Sparkfun).OUT2B, U4.MIDI_OUT
  N11: Easy_Driver_(Sparkfun).OUT1A, U4.MIDI_IN
  N12: Easy_Driver_(Sparkfun).OUT1B, U4.NC2
  N13: Lipo_2cells_(7_4V).GND, S1.leg1
  N14: Stepper_1_8°.A, U3.NC2
  N15: Stepper_1_8°.C, U3.MIDI_IN
  N16: Stepper_1_8°.B, U3.MIDI_OUT
  N17: Stepper_1_8°.D, U3.NC3
  N18: Joystick_+_Push_bt.GND, U2.NC3
  N19: Joystick_+_Push_bt.SEL, U2.MIDI_OUT
  N20: Joystick_+_Push_bt.HORZ, U2.MIDI_IN
  N21: Joystick_+_Push_bt.VCC, U2.NC2
